// Digital circuit P8D16A_2A main.dig as structural Verilog
module P8D16A_2A_main (
  input  clk
);

  wire button_1_out, clock_1_clk, dipswitch_1_out, undriven;

  LED HLT (.in(undriven));
  DipSwitch #(.dipDefault("true")) dipswitch_1 (.out(dipswitch_1_out));
  Button button_1 (.out(button_1_out));
  Clock clock_1 (.HLT(undriven), .Clock(clk), .M_CLK(button_1_out), .M_E(dipswitch_1_out), .CLK(clock_1_clk));
  Multiplier8b multiplier8b_1 ();  // open: E, X0, X1, X2, X3, X4, X5, X6, X7, Y0, Y1, Y2, Y3, Y4, Y5, Y6, Y7, O0, O1, O2, O3, O4, O5, O6, O7, O8, O9, O10, O11, O12, O13, O14, O15, FO
endmodule
