// Digital circuit Instruction Decoder.dig as structural Verilog
module Instruction_Decoder (
  input  CLK,
  input  I0,
  input  I1,
  input  I2,
  input  I3,
  input  I4,
  input  I5,
  input  I6,
  input  I7,
  input  IRQ,
  input  INT,
  input  F0,
  input  FC,
  input  FO,
  input  FN,
  output D0,
  output D1,
  output D2,
  output D3,
  output D4,
  output D5,
  output D6,
  output D7,
  output ALUE,
  output ALU_B,
  output ALUC,
  output ALUADD,
  output ALUAND,
  output ALUOR,
  output ALUNOT,
  output ALUXOR,
  output ALUSL,
  output ALUSR,
  output ALURL,
  output ALURR,
  output AR,
  output AW,
  output XR,
  output XW,
  output YR,
  output YW,
  output ZR,
  output ZW,
  output PCE,
  output PCHR,
  output PCHW,
  output PCLR,
  output PCLW,
  output SPR,
  output SPW,
  output SPINC,
  output SPDEC,
  output OHR,
  output OHW,
  output OLR,
  output OLW,
  output MAWL,
  output MAWH,
  output INTACK,
  output HLT,
  output MR,
  output MW,
  output ABOUT,
  output DBOUT,
  output DBIN
);

  wire flagregister_1_o0, flagsregister4b_1_o0, flagsregister4b_1_o1, flagsregister4b_1_o2,
       flagsregister4b_1_o3, interrupthandler_1_p8, not_1_out, not_2_out, not_3_out, not_4_out, or_1_out,
       or_2_out, or_3_out, or_4_out;
  wire [10:0] counter_1_out;
  wire [52:2] driver_1_out;
  wire [55:0] interrupthandler_1_p9, rom_1_d;

  or or_1 (or_1_out, I0, FC);
  or or_2 (or_2_out, I1, FN);
  or or_3 (or_3_out, I2, F0);
  or or_4 (or_4_out, I3, FO);
  not not_1 (not_1_out, CLK);
  Counter #(.Bits(3)) counter_1 (
    .en(not_1_out), .C(not_1_out), .clr(driver_1_out[52]), .out(counter_1_out[2:0]));  // open: ovf
  not not_2 (not_2_out, CLK);
  Register I (
    .CLK(CLK), .E(1'b1), .R(1'b1), .W(driver_1_out[35]), .D0(I0), .D1(I1), .D2(I2), .D3(I3), .D4(I4),
    .D5(I5), .D6(I6), .D7(I7), .O0(counter_1_out[3]), .O1(counter_1_out[4]), .O2(counter_1_out[5]),
    .O3(counter_1_out[6]), .O4(counter_1_out[7]), .O5(counter_1_out[8]), .O6(counter_1_out[9]),
    .O7(counter_1_out[10]));
  FlagsRegister4b flagsregister4b_1 (
    .CLK(not_2_out), .F0(or_1_out), .S0(driver_1_out[39]), .R0(driver_1_out[38]), .E0(driver_1_out[40]),
    .F1(or_2_out), .S1(1'b0), .R1(1'b0), .E1(driver_1_out[42]), .F2(or_3_out), .S2(1'b0), .R2(1'b0),
    .E2(driver_1_out[43]), .F3(or_4_out), .S3(1'b0), .R3(1'b0), .E3(driver_1_out[44]),
    .O0(flagsregister4b_1_o0), .O1(flagsregister4b_1_o1), .O2(flagsregister4b_1_o2), .O3(flagsregister4b_1_o3));
  FlagRegister flagregister_1 (
    .CLK(not_2_out), .F0(I4), .S0(driver_1_out[46]), .R0(driver_1_out[45]), .E0(driver_1_out[47]),
    .O0(flagregister_1_o0));
  // InterruptHandler interrupthandler_1: pin names not known; wires that end beside it: counter_1_out[0], counter_1_out[1], counter_1_out[2], INT, IRQ, flagregister_1_o0, INTACK, interrupthandler_1_p8, interrupthandler_1_p9
  ROM #(.AddrBits(11), .Bits(56)) rom_1 (.A(counter_1_out), .sel(1'b1), .D(rom_1_d));
  assign {DBIN, DBOUT, ABOUT, driver_1_out[52], HLT, INTACK, IRQ, driver_1_out[48:38], MW, MR, driver_1_out[35], MAWH, MAWL, OLW, OLR, OHW, OHR, SPDEC, SPINC, SPW, SPR, PCLW, PCLR, PCHW, PCHR, PCE, ZW, ZR, YW, YR, XW, XR, AW, AR, ALURR, ALURL, ALUSR, ALUSL, ALUXOR, ALUNOT, ALUOR, ALUAND, ALUADD, driver_1_out[2], ALU_B, ALUE} = not_3_out ? rom_1_d : 56'bz;  // Driver driver_1
  not not_3 (not_3_out, interrupthandler_1_p8);
  assign {DBIN, DBOUT, ABOUT, driver_1_out[52], HLT, INTACK, IRQ, driver_1_out[48:38], MW, MR, driver_1_out[35], MAWH, MAWL, OLW, OLR, OHW, OHR, SPDEC, SPINC, SPW, SPR, PCLW, PCLR, PCHW, PCHR, PCE, ZW, ZR, YW, YR, XW, XR, AW, AR, ALURR, ALURL, ALUSR, ALUSL, ALUXOR, ALUNOT, ALUOR, ALUAND, ALUADD, driver_1_out[2], ALU_B, ALUE} = interrupthandler_1_p8 ? interrupthandler_1_p9 : 56'bz;  // Driver driver_2
  PinControl8b pincontrol8b_1 (
    .E(driver_1_out[48]), .D0(flagsregister4b_1_o3), .D1(flagsregister4b_1_o2), .D2(flagsregister4b_1_o1),
    .D3(flagsregister4b_1_o0), .D4(flagregister_1_o0), .D5(1'b0), .D6(1'b0), .D7(1'b0), .O0(D0), .O1(D1),
    .O2(D2), .O3(D3), .O4(D4), .O5(D5), .O6(D6), .O7(D7));
  assign ALUC = not_4_out ? driver_1_out[2] : 1'bz;  // Driver driver_3
  not not_4 (not_4_out, driver_1_out[41]);
  assign ALUC = driver_1_out[41] ? flagsregister4b_1_o0 : 1'bz;  // Driver driver_4

  // Notes on the sheet:
  //   IW
  //   IMF E/S/R
  //   VF E
  //   0F E
  //   NF E
  //   CF E/S/R
  //   SCF
  //   CCF
  //   ECF
  //   ENF
  //   EZF
  //   EVF
  //   SIMF
  //   CIMF
  //   EIMF
  //   ALU
  //   Reg
  //   MEM
  //   F/INT
  //   MISC
  //   FTB
  //   CC
  //   SCF
  //   CCF
  //   ECF
  //   OCF
  //   ENF
  //   EZF
  //   EVF
  //   SIMF
  //   CIMF
  //   EIMF
  //   IRQ
endmodule
